# Fritzing sketch Water level sensor sketch (saved by Fritzing 0.9.3b)
breadboards: 1

parts:
  Water_Level_Sensor1 = Water Level Sensor
  Part1 = Arduino Uno (Rev3)
  LED1 = LED - 5mm [color="Orange (620nm)" package="5 mm [THT]"]
  LED2 = LED - 5mm [color="Red (633nm)" package="5 mm [THT]"]
  LED3 = LED - 5mm [color="Green (555nm)" package="5 mm [THT]"]
  R1 = Resistor [tolerance=±5% resistance=220 package=THT]
  R2 = Resistor [tolerance=±5% resistance=220 package=THT]
  R3 = Resistor [tolerance=±5% resistance=220 package=THT]

nets:
  N1: Water_Level_Sensor1.SIG, Part1.A2
  N2: Water_Level_Sensor1.VCC, Part1.D13/SCK
  GND: Water_Level_Sensor1.GND, Part1.GND, LED1.cathode, LED2.cathode
  N3: Part1.D2, R1.Pin_1
  N4: Part1.D5_PWM, R2.Pin_1
  N5: Part1.D7, R3.Pin_1
  N6: LED1.anode, R2.Pin_0
  N7: LED2.anode, R1.Pin_0
  N8: LED3.anode, R3.Pin_0

custom parts:
  Water Level Sensor: A water level sensor. This sensor operates at 3V to 5V. The Sig (signal) pin outputs an analogue signal that is in proportion to the amount of water in contact with the sensor.
